// Logisim project VLIW.circ as structural Verilog
module ProgramCounter (
  input  [7:0] data,
  input  Clk,
  input  Reset,
  output [7:0] Pc_mais_1,
  output [7:0] Pc_out
);

  Register register_1 (.D(data), .en(1'b1), .clk(Clk), .Q(Pc_out), .clr(Reset));
  Adder adder_1 (.a(Pc_out), .b(8'h4), .out(Pc_mais_1));  // open: cin, cout
endmodule

module Main (
  input  in_1,
  input  MANUAL_RESET,
  input  in_3
);

  wire and_1_out, and_2_out, BOZI, BOZR, CLK, JR, MEM_OR_ULA, MOVH, MOVL, NOP_1, NOP_2, NOP_3, NOP_4,
       or_1_out, or_2_out, or_3_out, or_4_out, R0_ZERO, RA_ZERO, W_MEM, WE_1, WE_3, WE_4;
  wire [2:0] OP_ULA_3, OP_ULA_4;
  wire [3:0] IMM_1, IMM_2;
  wire [7:0] LU_RESULT_1, LU_RESULT_2, LU_RESULT_3, LU_RESULT_4, MEM_OUT, multiplexer_1_out,
       multiplexer_2_out, multiplexer_3_out, PC, Pc_mais_1, R0_OUT, RA_1_OUT, RA_2_OUT, RA_3_OUT, RA_4_OUT,
       RB_1_OUT, RB_2_OUT, RB_3_OUT, RB_4_OUT, rom_1_p4, rom_1_p5;
  wire [7:4] rom_1_p2, rom_1_p3;

  or or_1 (or_1_out, BOZR, JR);
  Multiplexer #(.width(8)) multiplexer_1 (.in0(LU_RESULT_2), .in1(RB_1_OUT), .out(multiplexer_1_out), .sel(or_1_out));
  and and_1 (and_1_out, R0_ZERO, BOZI);
  and and_2 (and_2_out, RA_ZERO, BOZR);
  or or_2 (or_2_out, and_1_out, JR, and_2_out);
  Multiplexer #(.width(8)) multiplexer_2 (
    .in0(Pc_mais_1), .in1(multiplexer_1_out), .out(multiplexer_2_out), .sel(or_2_out));
  or or_3 (or_3_out, in_3, MANUAL_RESET);
  ProgramCounter programcounter_1 (
    .data(multiplexer_2_out), .Clk(CLK), .Reset(or_3_out), .Pc_mais_1(Pc_mais_1), .Pc_out(PC));
  // ROM #(.line("quad")) rom_1: pin names not known; wires that end beside it: PC, {rom_1_p2, IMM_1}, {rom_1_p3, IMM_2}, rom_1_p4, rom_1_p5
  Clock clock_1 (.out(CLK));
  ROM #(.addrWidth(4), .dataWidth(4)) rom_2 (.addr(rom_1_p3), .data({NOP_2, BOZR, BOZI, JR}));
  ROM #(.addrWidth(4), .dataWidth(6)) rom_3 (.addr(rom_1_p2), .data({NOP_1, MOVH, WE_1, W_MEM, MOVL, MEM_OR_ULA}));
  Multiplexer #(.width(8)) multiplexer_3 (.in0(LU_RESULT_1), .in1(MEM_OUT), .out(multiplexer_3_out), .sel(MEM_OR_ULA));
  or or_4 (or_4_out, in_1, in_3);
  banco_reg banco_reg_1 (
    .NOP_1(NOP_1), .NOP_3(NOP_3), .NOP_4(NOP_4), .Reset(or_4_out), .CLK(CLK), .MOVH(MOVH), .MOVL(MOVL),
    .RB_1(IMM_1[1:0]), .RB_2(IMM_2[1:0]), .RB_3(rom_1_p4[1:0]), .RB_4(rom_1_p5[1:0]),
    .DATA_1(multiplexer_3_out), .DATA_3(LU_RESULT_3), .DATA_4(LU_RESULT_4), .RA_1(IMM_1[3:2]),
    .RA_2(IMM_2[3:2]), .RA_3(rom_1_p4[3:2]), .RA_4(rom_1_p5[3:2]), .WE_1(WE_1), .WE_3(WE_3), .WE_4(WE_4),
    .RA_2_OUT(RA_2_OUT), .RA_3_OUT(RA_3_OUT), .RA_4_OUT(RA_4_OUT), .RA_1_OUT(RA_1_OUT), .RO_OUT(R0_OUT),
    .RB_2_OUT(RB_2_OUT), .RB_3_OUT(RB_3_OUT), .RB_4_OUT(RB_4_OUT), .RB_1_OUT(RB_1_OUT));
  ROM #(.addrWidth(4), .dataWidth(5)) rom_4 (.addr(rom_1_p4[7:4]), .data({NOP_3, OP_ULA_3, WE_3}));
  ROM #(.addrWidth(4), .dataWidth(5)) rom_5 (.addr(rom_1_p5[7:4]), .data({NOP_4, OP_ULA_4, WE_4}));
  LU_DATA lu_data_1 (.MOVL(MOVL), .R0(R0_OUT), .IMM(IMM_1), .DATA(LU_RESULT_1));
  LU_BRANCH lu_branch_1 (
    .IMM(IMM_2), .RA(RA_2_OUT), .R0(R0_OUT), .PC(PC), .PC_PLUS_IMM(LU_RESULT_2), .RA_ZERO(RA_ZERO),
    .R0_ZERO(R0_ZERO));
  ULA ula_1 (.op_ula(OP_ULA_3), .RA(RA_3_OUT), .RB(RB_3_OUT), .D(LU_RESULT_3));
  ULA ula_2 (.op_ula(OP_ULA_4), .RA(RA_4_OUT), .RB(RB_4_OUT), .D(LU_RESULT_4));
  RAM #(.asyncread("true")) ram_1 (.addr(RB_1_OUT), .we(W_MEM), .oe(1'b1), .clk(CLK), .din(RA_1_OUT), .dout(MEM_OUT));

  // Other names for the same wires on the sheet: RESET = in_3

  // Notes on the sheet:
  //   contents of rom_1 (hex, n*v repeats v):
  //   71 5*f0 84 88 f0 f0 94 bb f0 f0 c6 d2 f0 f0 f0 d2 62 f0 f0 f0 60 f0 f0 f0 58 f0 f0 f0 4c f0 f0 f0
  //   contents of rom_2 (hex, n*v repeats v):
  //   4 2 1 12*0 8
  //   contents of rom_3 (hex, n*v repeats v):
  //   4*0 9 4 18 a 7*0 20
  //   contents of rom_4 (hex, n*v repeats v):
  //   8*0 1 3 0 5 7 9 b 10
  //   contents of rom_5 (hex, n*v repeats v):
  //   8*0 1 3 0 5 7 9 b 10
endmodule

module banco_reg (
  input  WE_1,
  input  NOP_1,
  input  NOP_3,
  input  WE_3,
  input  NOP_4,
  input  Reset,
  input  CLK,
  input  WE_4,
  input  MOVH,
  input  MOVL,
  input  [1:0] RA_1,
  input  [1:0] RA_2,
  input  [1:0] RA_3,
  input  [1:0] RA_4,
  input  [1:0] RB_1,
  input  [1:0] RB_2,
  input  [1:0] RB_3,
  input  [1:0] RB_4,
  input  [7:0] DATA_1,
  input  [7:0] DATA_3,
  input  [7:0] DATA_4,
  output [7:0] RA_1_OUT,
  output [7:0] RB_1_OUT,
  output [7:0] RA_2_OUT,
  output [7:0] RB_2_OUT,
  output [7:0] RA_3_OUT,
  output [7:0] RB_3_OUT,
  output [7:0] RA_4_OUT,
  output [7:0] RB_4_OUT,
  output [7:0] RO_OUT
);

  wire and_1_out, demultiplexer_1_out0, not_1_out, or_1_out, or_7_out, or_8_out, or_9_out, or_10_out,
       or_11_out, or_12_out, W_R0_1, W_R0_3, W_R0_4, W_R1_1, W_R1_3, W_R1_4, W_R2_1, W_R2_3, W_R2_4, W_R3_1,
       W_R3_3, W_R3_4;
  wire [7:0] D_R0_1, D_R0_3, D_R0_4, D_R1_1, D_R1_3, D_R1_4, D_R2_1, D_R2_3, D_R2_4, D_R3_1, D_R3_3, D_R3_4,
       demultiplexer_4_out0, multiplexer_1_out, multiplexer_2_out, multiplexer_3_out, or_2_out, or_3_out,
       or_4_out, or_5_out, R1, R2, R3;

  or or_1 (or_1_out, MOVL, MOVH);
  not not_1 (not_1_out, or_1_out);
  and and_1 (and_1_out, not_1_out, WE_1);
  Demultiplexer #(.select(2)) demultiplexer_1 (
    .out0(demultiplexer_1_out0), .out1(W_R1_1), .out2(W_R2_1), .out3(W_R3_1), .in(and_1_out), .sel(RA_1));
  Demultiplexer #(.select(2)) demultiplexer_2 (
    .out0(W_R0_3), .out1(W_R1_3), .out2(W_R2_3), .out3(W_R3_3), .in(WE_3), .sel(RA_3));
  Demultiplexer #(.select(2)) demultiplexer_3 (
    .out0(W_R0_4), .out1(W_R1_4), .out2(W_R2_4), .out3(W_R3_4), .in(WE_4), .sel(RA_4));
  assign or_2_out = D_R0_1 | D_R0_3 | D_R0_4;  // OR_Gate or_2, 8 bits wide
  assign or_3_out = D_R1_1 | D_R1_3 | D_R1_4;  // OR_Gate or_3, 8 bits wide
  assign or_4_out = D_R2_1 | D_R2_3 | D_R2_4;  // OR_Gate or_4, 8 bits wide
  assign or_5_out = D_R3_1 | D_R3_3 | D_R3_4;  // OR_Gate or_5, 8 bits wide
  or or_6 (W_R0_1, MOVH, demultiplexer_1_out0, MOVL);
  or or_7 (or_7_out, W_R0_1, W_R0_3, W_R0_4);
  or or_8 (or_8_out, W_R1_1, W_R1_3, W_R1_4);
  or or_9 (or_9_out, W_R2_1, W_R2_3, W_R2_4);
  or or_10 (or_10_out, W_R3_1, W_R3_3, W_R3_4);
  Register R0 (.D(or_2_out), .en(or_7_out), .clk(CLK), .Q(RO_OUT), .clr(Reset));
  Register u_R1 (.D(or_3_out), .en(or_8_out), .clk(CLK), .Q(R1), .clr(Reset));
  Register u_R2 (.D(or_4_out), .en(or_9_out), .clk(CLK), .Q(R2), .clr(Reset));
  Register u_R3 (.D(or_5_out), .en(or_10_out), .clk(CLK), .Q(R3), .clr(Reset));
  or or_11 (or_11_out, MOVL, NOP_1, MOVH);
  Multiplexer #(.width(8)) multiplexer_1 (.in0(DATA_1), .in1({8{1'b0}}), .out(multiplexer_1_out), .sel(or_11_out));
  Demultiplexer #(.select(2), .width(8)) demultiplexer_4 (
    .out0(demultiplexer_4_out0), .out1(D_R1_1), .out2(D_R2_1), .out3(D_R3_1), .in(multiplexer_1_out),
    .sel(RA_1));
  Multiplexer #(.width(8)) multiplexer_2 (.in0(DATA_3), .in1({8{1'b0}}), .out(multiplexer_2_out), .sel(NOP_3));
  Demultiplexer #(.select(2), .width(8)) demultiplexer_5 (
    .out0(D_R0_3), .out1(D_R1_3), .out2(D_R2_3), .out3(D_R3_3), .in(multiplexer_2_out), .sel(RA_3));
  Multiplexer #(.width(8)) multiplexer_3 (.in0(DATA_4), .in1({8{1'b0}}), .out(multiplexer_3_out), .sel(NOP_4));
  Demultiplexer #(.select(2), .width(8)) demultiplexer_6 (
    .out0(D_R0_4), .out1(D_R1_4), .out2(D_R2_4), .out3(D_R3_4), .in(multiplexer_3_out), .sel(RA_4));
  or or_12 (or_12_out, MOVH, MOVL);
  Multiplexer #(.select(2), .width(8)) multiplexer_4 (
    .in0(RO_OUT), .in1(R1), .in2(R2), .in3(R3), .out(RA_1_OUT), .sel(RA_1));
  Multiplexer #(.select(2), .width(8)) multiplexer_5 (
    .in0(RO_OUT), .in1(R1), .in2(R2), .in3(R3), .out(RA_2_OUT), .sel(RA_2));
  Multiplexer #(.select(2), .width(8)) multiplexer_6 (
    .in0(RO_OUT), .in1(R1), .in2(R2), .in3(R3), .out(RA_3_OUT), .sel(RA_3));
  Multiplexer #(.select(2), .width(8)) multiplexer_7 (
    .in0(RO_OUT), .in1(R1), .in2(R2), .in3(R3), .out(RA_4_OUT), .sel(RA_4));
  Multiplexer #(.width(8)) multiplexer_8 (.in0(demultiplexer_4_out0), .in1(DATA_1), .out(D_R0_1), .sel(or_12_out));
  Multiplexer #(.select(2), .width(8)) multiplexer_9 (
    .in0(RO_OUT), .in1(R1), .in2(R2), .in3(R3), .out(RB_1_OUT), .sel(RB_1));
  Multiplexer #(.select(2), .width(8)) multiplexer_10 (
    .in0(RO_OUT), .in1(R1), .in2(R2), .in3(R3), .out(RB_2_OUT), .sel(RB_2));
  Multiplexer #(.select(2), .width(8)) multiplexer_11 (
    .in0(RO_OUT), .in1(R1), .in2(R2), .in3(R3), .out(RB_3_OUT), .sel(RB_3));
  Multiplexer #(.select(2), .width(8)) multiplexer_12 (
    .in0(RO_OUT), .in1(R1), .in2(R2), .in3(R3), .out(RB_4_OUT), .sel(RB_4));

  // Other names for the same wires on the sheet: CLK_t = CLK; R0[7:0] = RO_OUT; R_t = Reset
endmodule

module ULA (
  input  [7:0] RA,
  input  [7:0] RB,
  input  [2:0] op_ula,
  output [7:0] D
);

  wire comparator_1_eq;
  wire [2:0] bit_extender_1_out;
  wire [7:0] adder_1_out, bit_extender_2_out, not_1_out, or_1_out, shifter_1_out, shifter_2_out,
       subtractor_1_out, undriven;

  Bit_Extender #(.out_width(3)) bit_extender_1 (.in(RB), .out(bit_extender_1_out));
  Adder adder_1 (.a(RA), .b(RB), .out(adder_1_out));  // open: cin, cout
  Subtractor subtractor_1 (.a(RA), .b(RB), .out(subtractor_1_out));  // open: bin, bout
  assign or_1_out = RA | RB;  // OR_Gate or_1, 8 bits wide
  assign not_1_out = ~RB;  // NOT_Gate not_1, 8 bits wide
  Shifter shifter_1 (.in(RA), .\dist (bit_extender_1_out), .out(shifter_1_out));
  Shifter #(.shift("lr")) shifter_2 (.in(RA), .\dist (bit_extender_1_out), .out(shifter_2_out));
  Multiplexer #(.select(3), .width(8)) multiplexer_1 (
    .in0(adder_1_out), .in1(subtractor_1_out), .in2(or_1_out), .in3(not_1_out), .in4(shifter_1_out),
    .in5(shifter_2_out), .in6({8{1'b0}}), .in7({8{1'b0}}), .out(D), .sel(op_ula));
  Comparator comparator_1 (.a({8{1'b0}}), .b(undriven), .eq(comparator_1_eq));  // open: gt, lt
  assign bit_extender_2_out = {{7{1'b0}}, comparator_1_eq};  // Bit_Extender bit_extender_2
endmodule

module branches (
  input  [31:0] rs1,
  input  [31:0] rs2,
  input  B,
  input  [1:0] B_in,
  output B_out
);

  wire comparator_1_eq, comparator_1_gt, comparator_1_lt, not_1_out, or_1_out;

  Comparator #(.width(32)) comparator_1 (
    .a(rs1), .b(rs2), .gt(comparator_1_gt), .eq(comparator_1_eq), .lt(comparator_1_lt));
  or or_1 (or_1_out, comparator_1_gt, comparator_1_eq);
  not not_1 (not_1_out, comparator_1_eq);
  Multiplexer #(.enable("true"), .select(2)) multiplexer_1 (
    .in0(comparator_1_eq), .in1(comparator_1_lt), .in2(not_1_out), .in3(or_1_out), .out(B_out), .sel(B_in),
    .en(B));
endmodule

module dual_port_ram (
  input  [7:0] addr,
  input  [7:0] pc,
  input  [7:0] d,
  input  w,
  output [7:0] instr,
  output [7:0] data
);

  wire clock_1_out, or_1_out;
  wire [7:0] multiplexer_1_out;

  Clock clock_1 (.out(clock_1_out));
  or or_1 (or_1_out, w, clock_1_out);
  Multiplexer #(.width(8)) multiplexer_1 (.in0(addr), .in1(pc), .out(multiplexer_1_out), .sel(clock_1_out));
  RAM #(.asyncread("true")) ram_1 (
    .addr(multiplexer_1_out), .we(or_1_out), .oe(1'b1), .clk(clock_1_out), .din(d), .dout(data));
  Register #(.trigger("falling")) pcbuf (.D(data), .en(1'b1), .clk(clock_1_out), .Q(instr));  // open: clr
endmodule

module LU_BRANCH (
  input  [7:0] RA,
  input  [7:0] R0,
  input  [7:0] PC,
  input  [3:0] IMM,
  output RA_ZERO,
  output R0_ZERO,
  output [7:0] PC_PLUS_IMM
);

  wire [7:0] bit_extender_1_out, multiplier_1_out;

  Comparator comparator_1 (.a(RA), .b({8{1'b0}}), .eq(RA_ZERO));  // open: gt, lt
  Comparator comparator_2 (.a(R0), .b({8{1'b0}}), .eq(R0_ZERO));  // open: gt, lt
  assign bit_extender_1_out = {{4{IMM[3]}}, IMM};  // Bit_Extender bit_extender_1
  Multiplier multiplier_1 (.a(bit_extender_1_out), .b(8'h4), .out(multiplier_1_out));  // open: cin, cout
  Adder adder_1 (.a(PC), .b(multiplier_1_out), .out(PC_PLUS_IMM));  // open: cin, cout
endmodule

module LU_DATA (
  input  [3:0] IMM,
  input  MOVL,
  input  [7:0] R0,
  output [7:0] DATA
);

  wire [7:0] adder_1_out, adder_2_out, bit_extender_1_out, bit_extender_2_out, bit_extender_3_out,
       shifter_1_out, shifter_2_out;

  assign bit_extender_1_out = {{4{1'b0}}, R0[3:0]};  // Bit_Extender bit_extender_1
  assign bit_extender_2_out = {{4{1'b0}}, R0[7:4]};  // Bit_Extender bit_extender_2
  assign bit_extender_3_out = {{4{1'b0}}, IMM};  // Bit_Extender bit_extender_3
  Shifter shifter_1 (.in(bit_extender_3_out), .\dist (3'b100), .out(shifter_1_out));
  Shifter shifter_2 (.in(bit_extender_2_out), .\dist (3'b100), .out(shifter_2_out));
  Adder adder_1 (.a(bit_extender_1_out), .b(shifter_1_out), .out(adder_1_out));  // open: cin, cout
  Adder adder_2 (.a(bit_extender_3_out), .b(shifter_2_out), .out(adder_2_out));  // open: cin, cout
  Multiplexer #(.width(8)) multiplexer_1 (.in0(adder_1_out), .in1(adder_2_out), .out(DATA), .sel(MOVL));
endmodule
