// Logisim project Vetorial.circ as structural Verilog: 11 circuits, main circuit ProgramCounter
module ProgramCounter (
  input  [7:0] data,
  input  Clk,
  input  Reset,
  output [7:0] Pc_mais_1,
  output [7:0] Pc_out
);

  Register register_1 (.D(data), .en(1'b1), .clk(Clk), .Q(Pc_out), .clr(Reset));
  Adder adder_1 (.a(Pc_out), .b(8'h1), .out(Pc_mais_1));  // open: cin, cout
endmodule

module Main (
  input  in_1,
  input  in_2,
  input  MANUAL_RESET,
  input  in_4,
  input  in_5,
  input  in_6,
  input  in_7
);

  wire and_1_out, BOZR, CLK, LD, MOV, or_1_out, or_2_out, or_3_out, or_4_out, or_5_out, or_6_out, RA_ZERO,
       ST_SR, ST_V, WE_SR, WE_V;
  wire [1:0] RA_CHOICE;
  wire [2:0] OP_ULA;
  wire [3:0] IMM, OPCODE;
  wire [7:0] MEM_OUT_0, MEM_OUT_1, MEM_OUT_2, MEM_OUT_3, MEM_OUT_SR, multiplexer_1_out, multiplexer_3_out,
       multiplexer_4_out, multiplexer_5_out, multiplexer_6_out, multiplexer_7_out, PC, PC_MAIS_1, R1_0_OUT,
       R1_1_OUT, R1_2_OUT, R1_3_OUT, R1_OUT_SR, RA_0_OUT, RA_1_OUT, RA_2_OUT, RA_3_OUT, RA_OUT_SR, RB_0_OUT,
       RB_1_OUT, RB_2_OUT, RB_3_OUT, RB_OUT_SR, ULA_RESULT_0, ULA_RESULT_1, ULA_RESULT_2, ULA_RESULT_3,
       ULA_RESULT_SR;

  and and_1 (and_1_out, RA_ZERO, BOZR);
  Multiplexer #(.width(8)) multiplexer_1 (.in0(PC_MAIS_1), .in1(RB_OUT_SR), .out(multiplexer_1_out), .sel(and_1_out));
  or or_1 (or_1_out, in_4, MANUAL_RESET);
  ProgramCounter programcounter_1 (
    .data(multiplexer_1_out), .Clk(CLK), .Reset(or_1_out), .Pc_mais_1(PC_MAIS_1), .Pc_out(PC));
  ROM rom_1 (.addr(PC), .data({OPCODE, IMM}));
  Clock clock_1 (.out(CLK));
  CONTROL_UNIT control_unit_1 (
    .BIT_1(OPCODE[0]), .BIT_2(OPCODE[1]), .BIT_3(OPCODE[2]), .BIT_4(OPCODE[3]), .MOV(MOV), .LOAD(LD),
    .BRANCH(BOZR), .OP_ULA(OP_ULA), .STORE_V(ST_V), .STORE_SR(ST_SR), .WE_V(WE_V), .WE_SR(WE_SR));
  Multiplexer #(.width(2)) multiplexer_2 (.in0(IMM[3:2]), .in1(2'b01), .out(RA_CHOICE), .sel(MOV));
  RAM #(.asyncread("true")) ram_1 (
    .addr(RB_OUT_SR), .we(ST_SR), .oe(1'b1), .clk(CLK), .din(RA_OUT_SR), .dout(MEM_OUT_SR));
  or or_2 (or_2_out, in_1, in_4);
  banco_reg banco_reg_1 (
    .WE(WE_SR), .Reset(or_2_out), .CLK(CLK), .DATA(multiplexer_3_out), .RA(RA_CHOICE), .RB(IMM[1:0]),
    .RA_OUT(RA_OUT_SR), .RB_OUT(RB_OUT_SR), .R1_OUT(R1_OUT_SR));
  Multiplexer #(.width(8)) multiplexer_3 (.in0(ULA_RESULT_SR), .in1(MEM_OUT_SR), .out(multiplexer_3_out), .sel(LD));
  ULA ula_1 (
    .RA(RA_OUT_SR), .RB(RB_OUT_SR), .op_ula(OP_ULA), .R1(R1_OUT_SR), .IMM(IMM), .RA_ZERO(RA_ZERO),
    .ULA_RESULT(ULA_RESULT_SR));
  or or_3 (or_3_out, in_2, in_4);
  REG_BANK_VET_0 reg_bank_vet_0_1 (
    .WE(WE_V), .Reset(or_3_out), .CLK(CLK), .DATA(multiplexer_4_out), .RA(RA_CHOICE), .RB(IMM[1:0]),
    .RA_OUT(RA_0_OUT), .RB_OUT(RB_0_OUT), .R1_OUT(R1_0_OUT));
  Multiplexer #(.width(8)) multiplexer_4 (.in0(ULA_RESULT_0), .in1(MEM_OUT_0), .out(multiplexer_4_out), .sel(LD));
  or or_4 (or_4_out, in_5, in_4);
  REG_BANK_VET_1 reg_bank_vet_1_1 (
    .WE(WE_V), .Reset(or_4_out), .CLK(CLK), .DATA(multiplexer_5_out), .RA(RA_CHOICE), .RB(IMM[1:0]),
    .RA_OUT(RA_1_OUT), .RB_OUT(RB_1_OUT), .R1_OUT(R1_1_OUT));
  Multiplexer #(.width(8)) multiplexer_5 (.in0(ULA_RESULT_1), .in1(MEM_OUT_1), .out(multiplexer_5_out), .sel(LD));
  or or_5 (or_5_out, in_6, in_4);
  REG_BANK_VET_2 reg_bank_vet_2_1 (
    .WE(WE_V), .Reset(or_5_out), .CLK(CLK), .DATA(multiplexer_6_out), .RA(RA_CHOICE), .RB(IMM[1:0]),
    .RA_OUT(RA_2_OUT), .RB_OUT(RB_2_OUT), .R1_OUT(R1_2_OUT));
  Multiplexer #(.width(8)) multiplexer_6 (.in0(ULA_RESULT_2), .in1(MEM_OUT_2), .out(multiplexer_6_out), .sel(LD));
  or or_6 (or_6_out, in_7, in_4);
  REG_BANK_VET_3 reg_bank_vet_3_1 (
    .WE(WE_V), .Reset(or_6_out), .CLK(CLK), .DATA(multiplexer_7_out), .RA(RA_CHOICE), .RB(IMM[1:0]),
    .RA_OUT(RA_3_OUT), .RB_OUT(RB_3_OUT), .R1_OUT(R1_3_OUT));
  Multiplexer #(.width(8)) multiplexer_7 (.in0(ULA_RESULT_3), .in1(MEM_OUT_3), .out(multiplexer_7_out), .sel(LD));
  VETORIAL_ULA vetorial_ula_1 (
    .RA(RA_0_OUT), .RB(RB_0_OUT), .op_ula(OP_ULA), .R1(R1_0_OUT), .IMM(IMM), .ULA_RESULT(ULA_RESULT_0));
  VETORIAL_ULA vetorial_ula_2 (
    .RA(RA_1_OUT), .RB(RB_1_OUT), .op_ula(OP_ULA), .R1(R1_1_OUT), .IMM(IMM), .ULA_RESULT(ULA_RESULT_1));
  VETORIAL_ULA vetorial_ula_3 (
    .RA(RA_2_OUT), .RB(RB_2_OUT), .op_ula(OP_ULA), .R1(R1_2_OUT), .IMM(IMM), .ULA_RESULT(ULA_RESULT_2));
  VETORIAL_ULA vetorial_ula_4 (
    .RA(RA_3_OUT), .RB(RB_3_OUT), .op_ula(OP_ULA), .R1(R1_3_OUT), .IMM(IMM), .ULA_RESULT(ULA_RESULT_3));
  RAM #(.asyncread("true")) ram_2 (.addr(RB_0_OUT), .we(ST_V), .oe(1'b1), .clk(CLK), .din(RA_0_OUT), .dout(MEM_OUT_0));
  RAM #(.asyncread("true")) ram_3 (.addr(RB_1_OUT), .we(ST_V), .oe(1'b1), .clk(CLK), .din(RA_1_OUT), .dout(MEM_OUT_1));
  RAM #(.asyncread("true")) ram_4 (.addr(RB_2_OUT), .we(ST_V), .oe(1'b1), .clk(CLK), .din(RA_2_OUT), .dout(MEM_OUT_2));
  RAM #(.asyncread("true")) ram_5 (.addr(RB_3_OUT), .we(ST_V), .oe(1'b1), .clk(CLK), .din(RA_3_OUT), .dout(MEM_OUT_3));

  // Other names for the same wires on the sheet: RB[1:0] = IMM[1:0]; RA[1:0] = IMM[3:2]; RESET = in_4

  // Notes on the sheet:
  //   contents of rom_1 (hex, n*v repeats v):
  //   b1 c9 a1 cd cc de c8 9b 87
  //   INICIAR EM BORDA DE SUBIDA
endmodule

module banco_reg (
  input  WE,
  input  Reset,
  input  CLK,
  input  [1:0] RA,
  input  [1:0] RB,
  input  [7:0] DATA,
  output [7:0] R1_OUT,
  output [7:0] RA_OUT,
  output [7:0] RB_OUT
);

  wire W_R1, W_R2, W_R3;
  wire [7:0] R0, R2, R3;

  Register u_R0 (.D({8{1'b0}}), .en(1'b1), .clk(CLK), .Q(R0), .clr(Reset));
  Register R1 (.D(DATA), .en(W_R1), .clk(CLK), .Q(R1_OUT), .clr(Reset));
  Demultiplexer #(.select(2)) demultiplexer_1 (.out1(W_R1), .out2(W_R2), .out3(W_R3), .in(WE), .sel(RA));  // open: out0
  Register u_R2 (.D(DATA), .en(W_R2), .clk(CLK), .Q(R2), .clr(Reset));
  Register u_R3 (.D(DATA), .en(W_R3), .clk(CLK), .Q(R3), .clr(Reset));
  Multiplexer #(.select(2), .width(8)) multiplexer_1 (
    .in0(R0), .in1(R1_OUT), .in2(R2), .in3(R3), .out(RA_OUT), .sel(RA));
  Multiplexer #(.select(2), .width(8)) multiplexer_2 (
    .in0(R0), .in1(R1_OUT), .in2(R2), .in3(R3), .out(RB_OUT), .sel(RB));

  // Other names for the same wires on the sheet: CLK_t = CLK; R1[7:0] = R1_OUT; R_t = Reset
endmodule

module ULA (
  input  [3:0] IMM,
  input  [2:0] op_ula,
  input  [7:0] R1,
  input  [7:0] RA,
  input  [7:0] RB,
  output [7:0] ULA_RESULT,
  output RA_ZERO
);

  wire [7:0] adder_1_out, adder_2_out, adder_3_out, and_1_out, bit_extender_1_out, bit_extender_2_out,
       bit_extender_3_out, shifter_1_out, shifter_2_out, subtractor_1_out;

  assign bit_extender_1_out = {{4{1'b0}}, R1[3:0]};  // Bit_Extender bit_extender_1
  assign bit_extender_2_out = {{4{1'b0}}, R1[7:4]};  // Bit_Extender bit_extender_2
  assign bit_extender_3_out = {{4{1'b0}}, IMM};  // Bit_Extender bit_extender_3
  Shifter shifter_1 (.in(bit_extender_3_out), .\dist (3'b100), .out(shifter_1_out));
  Shifter shifter_2 (.in(bit_extender_2_out), .\dist (3'b100), .out(shifter_2_out));
  Adder adder_1 (.a(RA), .b(RB), .out(adder_1_out));  // open: cin, cout
  Subtractor subtractor_1 (.a(RA), .b(RB), .out(subtractor_1_out));  // open: bin, bout
  assign and_1_out = RA & RB;  // AND_Gate and_1, 8 bits wide
  Comparator comparator_1 (.a(RA), .b({8{1'b0}}), .eq(RA_ZERO));  // open: gt, lt
  Adder adder_2 (.a(bit_extender_1_out), .b(shifter_1_out), .out(adder_2_out));  // open: cin, cout
  Adder adder_3 (.a(bit_extender_3_out), .b(shifter_2_out), .out(adder_3_out));  // open: cin, cout
  Multiplexer #(.select(3), .width(8)) multiplexer_1 (
    .in2(adder_2_out), .in3(adder_3_out), .in4(adder_1_out), .in5(subtractor_1_out), .in6(and_1_out),
    .in7({8{1'b0}}), .out(ULA_RESULT), .sel(op_ula));  // open: in0, in1
endmodule

module dual_port_ram (
  input  [7:0] addr,
  input  [7:0] pc,
  input  [7:0] d,
  input  w,
  output [7:0] instr,
  output [7:0] data
);

  wire clock_1_out, or_1_out;
  wire [7:0] multiplexer_1_out;

  Clock clock_1 (.out(clock_1_out));
  or or_1 (or_1_out, w, clock_1_out);
  Multiplexer #(.width(8)) multiplexer_1 (.in0(addr), .in1(pc), .out(multiplexer_1_out), .sel(clock_1_out));
  RAM #(.asyncread("true")) ram_1 (
    .addr(multiplexer_1_out), .we(or_1_out), .oe(1'b1), .clk(clock_1_out), .din(d), .dout(data));
  Register #(.trigger("falling")) pcbuf (.D(data), .en(1'b1), .clk(clock_1_out), .Q(instr));  // open: clr
endmodule

module VETORIAL_ULA (
  input  [3:0] IMM,
  input  [2:0] op_ula,
  input  [7:0] R1,
  input  [7:0] RA,
  input  [7:0] RB,
  output [7:0] ULA_RESULT
);

  wire [7:0] adder_1_out, adder_2_out, adder_3_out, and_1_out, bit_extender_1_out, bit_extender_2_out,
       bit_extender_3_out, shifter_1_out, shifter_2_out, subtractor_1_out;

  assign bit_extender_1_out = {{4{1'b0}}, R1[3:0]};  // Bit_Extender bit_extender_1
  assign bit_extender_2_out = {{4{1'b0}}, R1[7:4]};  // Bit_Extender bit_extender_2
  assign bit_extender_3_out = {{4{1'b0}}, IMM};  // Bit_Extender bit_extender_3
  Shifter shifter_1 (.in(bit_extender_3_out), .\dist (3'b100), .out(shifter_1_out));
  Shifter shifter_2 (.in(bit_extender_2_out), .\dist (3'b100), .out(shifter_2_out));
  Adder adder_1 (.a(RA), .b(RB), .out(adder_1_out));  // open: cin, cout
  Subtractor subtractor_1 (.a(RA), .b(RB), .out(subtractor_1_out));  // open: bin, bout
  assign and_1_out = RA & RB;  // AND_Gate and_1, 8 bits wide
  Adder adder_2 (.a(bit_extender_1_out), .b(shifter_1_out), .out(adder_2_out));  // open: cin, cout
  Adder adder_3 (.a(bit_extender_3_out), .b(shifter_2_out), .out(adder_3_out));  // open: cin, cout
  Multiplexer #(.select(3), .width(8)) multiplexer_1 (
    .in2(adder_2_out), .in3(adder_3_out), .in4(adder_1_out), .in5(subtractor_1_out), .in6(and_1_out),
    .in7({8{1'b0}}), .out(ULA_RESULT), .sel(op_ula));  // open: in0, in1
endmodule

module REG_BANK_VET_0 (
  input  WE,
  input  Reset,
  input  CLK,
  input  [1:0] RA,
  input  [1:0] RB,
  input  [7:0] DATA,
  output [7:0] R1_OUT,
  output [7:0] RA_OUT,
  output [7:0] RB_OUT
);

  wire W_R1, W_R2, W_R3;
  wire [7:0] R0, R2, R3;

  Register #(.trigger("falling")) u_R0 (.D({8{1'b0}}), .en(1'b1), .clk(CLK), .Q(R0), .clr(Reset));
  Register R1 (.D(DATA), .en(W_R1), .clk(CLK), .Q(R1_OUT), .clr(Reset));
  Demultiplexer #(.select(2)) demultiplexer_1 (.out1(W_R1), .out2(W_R2), .out3(W_R3), .in(WE), .sel(RA));  // open: out0
  Register u_R2 (.D(DATA), .en(W_R2), .clk(CLK), .Q(R2), .clr(Reset));
  Register u_R3 (.D(DATA), .en(W_R3), .clk(CLK), .Q(R3), .clr(Reset));
  Multiplexer #(.select(2), .width(8)) multiplexer_1 (
    .in0(R0), .in1(R1_OUT), .in2(R2), .in3(R3), .out(RA_OUT), .sel(RA));
  Multiplexer #(.select(2), .width(8)) multiplexer_2 (
    .in0(R0), .in1(R1_OUT), .in2(R2), .in3(R3), .out(RB_OUT), .sel(RB));

  // Other names for the same wires on the sheet: CLK_t = CLK; R1[7:0] = R1_OUT; R_t = Reset
endmodule

module REG_BANK_VET_1 (
  input  WE,
  input  Reset,
  input  CLK,
  input  [1:0] RA,
  input  [1:0] RB,
  input  [7:0] DATA,
  output [7:0] R1_OUT,
  output [7:0] RA_OUT,
  output [7:0] RB_OUT
);

  wire W_R1, W_R2, W_R3;
  wire [7:0] R0, R2, R3;

  Register #(.trigger("falling")) u_R0 (.D(8'h1), .en(1'b1), .clk(CLK), .Q(R0), .clr(Reset));
  Register R1 (.D(DATA), .en(W_R1), .clk(CLK), .Q(R1_OUT), .clr(Reset));
  Demultiplexer #(.select(2)) demultiplexer_1 (.out1(W_R1), .out2(W_R2), .out3(W_R3), .in(WE), .sel(RA));  // open: out0
  Register u_R2 (.D(DATA), .en(W_R2), .clk(CLK), .Q(R2), .clr(Reset));
  Register u_R3 (.D(DATA), .en(W_R3), .clk(CLK), .Q(R3), .clr(Reset));
  Multiplexer #(.select(2), .width(8)) multiplexer_1 (
    .in0(R0), .in1(R1_OUT), .in2(R2), .in3(R3), .out(RA_OUT), .sel(RA));
  Multiplexer #(.select(2), .width(8)) multiplexer_2 (
    .in0(R0), .in1(R1_OUT), .in2(R2), .in3(R3), .out(RB_OUT), .sel(RB));

  // Other names for the same wires on the sheet: CLK_t = CLK; R1[7:0] = R1_OUT; R_t = Reset
endmodule

module REG_BANK_VET_2 (
  input  WE,
  input  Reset,
  input  CLK,
  input  [1:0] RA,
  input  [1:0] RB,
  input  [7:0] DATA,
  output [7:0] R1_OUT,
  output [7:0] RA_OUT,
  output [7:0] RB_OUT
);

  wire W_R1, W_R2, W_R3;
  wire [7:0] R0, R2, R3;

  Register #(.trigger("falling")) u_R0 (.D(8'h2), .en(1'b1), .clk(CLK), .Q(R0), .clr(Reset));
  Register R1 (.D(DATA), .en(W_R1), .clk(CLK), .Q(R1_OUT), .clr(Reset));
  Demultiplexer #(.select(2)) demultiplexer_1 (.out1(W_R1), .out2(W_R2), .out3(W_R3), .in(WE), .sel(RA));  // open: out0
  Register u_R2 (.D(DATA), .en(W_R2), .clk(CLK), .Q(R2), .clr(Reset));
  Register u_R3 (.D(DATA), .en(W_R3), .clk(CLK), .Q(R3), .clr(Reset));
  Multiplexer #(.select(2), .width(8)) multiplexer_1 (
    .in0(R0), .in1(R1_OUT), .in2(R2), .in3(R3), .out(RA_OUT), .sel(RA));
  Multiplexer #(.select(2), .width(8)) multiplexer_2 (
    .in0(R0), .in1(R1_OUT), .in2(R2), .in3(R3), .out(RB_OUT), .sel(RB));

  // Other names for the same wires on the sheet: CLK_t = CLK; R1[7:0] = R1_OUT; R_t = Reset
endmodule

module REG_BANK_VET_3 (
  input  WE,
  input  Reset,
  input  CLK,
  input  [1:0] RA,
  input  [1:0] RB,
  input  [7:0] DATA,
  output [7:0] R1_OUT,
  output [7:0] RA_OUT,
  output [7:0] RB_OUT
);

  wire W_R1, W_R2, W_R3;
  wire [7:0] R0, R2, R3;

  Register #(.trigger("falling")) u_R0 (.D(8'h3), .en(1'b1), .clk(CLK), .Q(R0), .clr(Reset));
  Register R1 (.D(DATA), .en(W_R1), .clk(CLK), .Q(R1_OUT), .clr(Reset));
  Demultiplexer #(.select(2)) demultiplexer_1 (.out1(W_R1), .out2(W_R2), .out3(W_R3), .in(WE), .sel(RA));  // open: out0
  Register u_R2 (.D(DATA), .en(W_R2), .clk(CLK), .Q(R2), .clr(Reset));
  Register u_R3 (.D(DATA), .en(W_R3), .clk(CLK), .Q(R3), .clr(Reset));
  Multiplexer #(.select(2), .width(8)) multiplexer_1 (
    .in0(R0), .in1(R1_OUT), .in2(R2), .in3(R3), .out(RA_OUT), .sel(RA));
  Multiplexer #(.select(2), .width(8)) multiplexer_2 (
    .in0(R0), .in1(R1_OUT), .in2(R2), .in3(R3), .out(RB_OUT), .sel(RB));

  // Other names for the same wires on the sheet: CLK_t = CLK; R1[7:0] = R1_OUT; R_t = Reset
endmodule

module CONTROL_UNIT (
  input  BIT_1,
  input  BIT_2,
  input  BIT_3,
  input  BIT_4,
  output MOV,
  output [2:0] OP_ULA,
  output LOAD,
  output WE_V,
  output BRANCH,
  output WE_SR,
  output STORE_V,
  output STORE_SR
);

  wire and_1_out, and_5_out, not_5_out, NOT_BIT_1, NOT_BIT_2, NOT_BIT_3, NOT_BIT_4, or_1_out, or_2_out;

  not not_1 (NOT_BIT_1, BIT_1);
  not not_2 (NOT_BIT_2, BIT_2);
  not not_3 (NOT_BIT_3, BIT_3);
  not not_4 (NOT_BIT_4, BIT_4);
  or or_1 (or_1_out, NOT_BIT_1, BIT_1);
  and and_1 (and_1_out, BIT_2, NOT_BIT_3);
  and and_2 (MOV, or_1_out, and_1_out);
  and and_3 (LOAD, NOT_BIT_1, NOT_BIT_2, NOT_BIT_3);
  and and_4 (BRANCH, BIT_1, BIT_2, BIT_3);
  and and_5 (and_5_out, BIT_1, NOT_BIT_2, NOT_BIT_3);
  or or_2 (or_2_out, BRANCH, and_5_out);
  not not_5 (not_5_out, or_2_out);
  and and_6 (STORE_V, BIT_4, and_5_out);
  and and_7 (STORE_SR, and_5_out, NOT_BIT_4);
  and and_8 (WE_V, BIT_4, not_5_out);
  and and_9 (WE_SR, not_5_out, NOT_BIT_4);

  assign OP_ULA = {BIT_3, BIT_2, BIT_1};
endmodule
